# Fritzing sketch Skema IoT (saved by Fritzing 0.8.7b)
breadboards: 1

parts:
  U1 = NodeMCU V1.0
  Part2 = KY-015 Temperature & Humidity Sensor Module [package="Breakout board"]
  U2 = LM2596 step down module
  4_Channel_Relay1 = 4 Channel Power Relay
  JACK1 = 2.1mm Barrel Jack with Terminal Block
  M1 = DC Motor
  Part3 = FC-28 Soil Hygrometer Module - Probe
  Part4 = FC-28 Soil Hygrometer Module

nets:
  N1: U1.D2, Part2.S
  3V3: U1.3V3, Part2.Vin, Part4.VCC
  GND: U1.GND, Part2.-, U2.IN-, U2.OUT-, 4_Channel_Relay1.GND, JACK1.NEG, M1.pin_2, Part4.GND
  N2: U1.D5, 4_Channel_Relay1.IN1
  VIN: U1.Vin, U2.OUT+, 4_Channel_Relay1.VCC, 4_Channel_Relay1.COM
  N3: U1.A0, Part4.AO
  N4: U2.IN+, JACK1.POS
  N5: 4_Channel_Relay1.NC, M1.Water_Pump_DC
  N6: Part3.POS, Part4.POS
  N7: Part3.NEG, Part4.NEG

custom parts:
  NodeMCU V1.0: ESP8266 based NodeMCU
  KY-015 Temperature & Humidity Sensor Module: KY-015 temperature and humidity sensor module, provides a low-latency serial interface to measure humidity and temperature.
  LM2596 step down module: LM2596 DC-DC step down power supply module 3 A.
  4 Channel Power Relay: A 4 channel power relay. The module operates at 5V.
  DC Motor: Your standard DC Motor
  FC-28 Soil Hygrometer Module - Probe: The FC-28 is a soil hygrometer module that uses the Texas Instruments LM393 comparator chip to provide an analog measurement of soil humidity.
  FC-28 Soil Hygrometer Module: The FC-28 is a soil hygrometer module that uses the Texas Instruments LM393 comparator chip to provide an analog measurement of soil humidity. The digital output is high when soil moisture is over a certain threshold, as determined by adjusting the potentiometer.
